# Fritzing sketch 220switch_bb (saved by Fritzing 0.7.12b)
breadboards: 1

parts:
  Arduino1 = Arduino
  K1 = Relay [part_number=FRS1B-S package=THT]

nets:
  N1: Arduino1.GND, K1.A
  N2: Arduino1.D13, K1.C1, K1.C2
