# Fritzing sketch button-piezo01 (saved by Fritzing 0.7.5b)
breadboards: 1

parts:
  Arduino1 = Arduino
  J1 = Piezo Speaker
  S1 = Pushbutton [package="[THT]"]
  R1 = Resistor [tolerance=±5% resistance=1k package=THT]

nets:
  N1: Arduino1.D11, J1.pin2
  N2: Arduino1.D2, S1.Pin_1, S1.Pin_2, R1.Pin_0
  N3: Arduino1.+5V, S1.Pin_3, S1.Pin_4
  N4: Arduino1.GND, J1.pin1, R1.Pin_1
