# Fritzing sketch tilt (saved by Fritzing 0.7.12b)
breadboards: 2

parts:
  Arduino2 = Arduino
  R2 = Resistor [tolerance=±5% resistance=1k package=THT]
  S3 = Tilt Switch [package=THT]
  LED1 = LED - 5mm [color="Red (633nm)" package="5 mm [THT]"]
  R3 = Resistor [tolerance=±5% resistance=470 package=THT]
  Arduino3 = Arduino
  R4 = Resistor [tolerance=±5% resistance=1k package=THT]
  S4 = Tilt Switch [package=THT]
  LED2 = LED - 5mm [color="Red (633nm)" package="5 mm [THT]"]
  R5 = Resistor [tolerance=±5% resistance=470 package=THT]

nets:
  N1: Arduino2.D11, R3.Pin_1
  N2: Arduino2.D2, R2.Pin_0, S3.Pin_2
  N3: Arduino2.+5V, S3.Pin_1
  N4: Arduino2.GND, LED1.cathode
  N5: LED1.anode, R3.Pin_0
  N6: Arduino3.GND, S4.Pin_1, LED2.cathode
  N7: Arduino3.D11, R5.Pin_1
  N8: Arduino3.D2, R4.Pin_0, S4.Pin_2
  N9: LED2.anode, R5.Pin_0
