# Fritzing sketch ldrpiezopot01 (saved by Fritzing 0.7.5b)
breadboards: 1

parts:
  Arduino1 = Arduino
  J1 = Piezo Speaker
  R1 = Resistor [tolerance=±5% resistance=1k package=THT]
  R2 = Photocell (LDR) [package=THT]
  R3 = Rotary Potentiometer (Small) [maximum_resistance=100kΩ]

nets:
  N1: Arduino1.D11, J1.pin2
  N2: Arduino1.+5V, R2.pin_0, R3.leg1
  N3: Arduino1.GND, J1.pin1, R1.Pin_1, R3.leg2
  N4: Arduino1.A0, R1.Pin_0, R2.pin_1
  N5: Arduino1.A1, R3.wiper
