# Fritzing sketch pir (saved by Fritzing 0.7.12b)
breadboards: 1

parts:
  R3 = Resistor [tolerance=±5% resistance=1k package=THT]
  U1 = mystery part, 3 pins [chip_label=? spacing=300mil]
  Arduino2 = Arduino

nets:
  N1: R3.Pin_0, U1.pin3, Arduino2.D2
  N2: R3.Pin_1, U1.pin1, Arduino2.+5V
  N3: U1.pin2, Arduino2.GND
