# Fritzing sketch sensor-flex (saved by Fritzing 0.7.12b)
breadboards: 1

parts:
  Arduino2 = Arduino
  R3 = Resistor [tolerance=±5% resistance=1k package=THT]
  R5 = Basic Flex Resistor

nets:
  N1: Arduino2.+5V, R5.Pin_2
  N2: Arduino2.GND, R3.Pin_0
  N3: Arduino2.A0, R5.pin_1
