# Fritzing sketch sensor-read-01 (saved by Fritzing 0.7.5b)
breadboards: 1

parts:
  Arduino1 = Arduino
  R1 = Resistor [tolerance=±5% resistance=1k package=THT]
  R2 = Photocell (LDR) [package=THT]

nets:
  N1: Arduino1.+5V, R2.pin_1
  N2: Arduino1.GND, R1.Pin_0
  N3: Arduino1.A0, R2.pin_0
