# Fritzing sketch sensor-read-03 (saved by Fritzing 0.7.12b)
breadboards: 1

parts:
  Arduino1 = Arduino
  R1 = Resistor [tolerance=±5% resistance=1k package=THT]
  R2 = Photocell (LDR) [package=THT]
  LED1 = LED - 5mm [color="Red (633nm)" package="5 mm [THT]"]
  R3 = Resistor [tolerance=±5% resistance=330 package=THT]

nets:
  N1: Arduino1.D11, R3.Pin_0
  N2: Arduino1.+5V, R2.pin_1
  N3: Arduino1.GND, R1.Pin_0, LED1.cathode
  N4: Arduino1.A0, R2.pin_0
  N5: LED1.anode, R3.Pin_1
